# Fritzing sketch iambic decoder (saved by Fritzing 0.9.10b)
stripboards: 2

parts:
  U1 = LM386 [package=dip08]  # not connected
  C1 = Electrolytic Capacitor top view [package="100 mil [THT, electrolytic]"]  # not connected
  R1 = Vertical Resistor [tolerance=±5% resistance=500k package=THT]  # not connected
  C2 = Electrolytic Capacitor [capacitance=10μF voltage=35V package="0605 [SMD, electrolytic]"]  # not connected
  MCU1 = Wemos Lolin32lite
  LCM1602_IIC1 = LCM1602 IIC [part_number="LCM1602 IIC" chip_label="LCM1602 IIC" package="DIP (Dual Inline) [THT]"]
  U2 = JST XH 3A Male [chip_label=? package=THT]
  SP1 = SPEAKER [package=pcb_mount_speaker]
  J5 = JST XH 2A male [form="♂ (male)" package=THT]
  U4 = JST XH 4A 2.54mm [package=THT]
  J6 = JST XH 2A male [form="♂ (male)" package=THT]  # not connected
  U6 = JST XH 3A Male [chip_label=? package=THT]  # not connected
  U7 = POT [knob_status=50% power=0.5W package=pot_mammoth]  # not connected
  R2 = Rotary Potentiometer (Large) [maximum_resistance=500kΩ knob_status=50% power=0.5W package=THT]
  U8 = AUDIO-JACK2 [package=audio-jack-3.5mm-smd]  # not connected
  U9 = AUDIO-JACK2 [package=audio-jack-3.5mm-smd]
  U10 = JST XH 3A Male [chip_label=? package=THT]

nets:
  N1: MCU1.pin_21, U9.RING, U10.pin2
  N2: MCU1.pin_22, U9.TIP, U10.pin1
  N3: LCM1602_IIC1.GND, U4.pin4
  N4: LCM1602_IIC1.VCC, U4.pin3
  N5: LCM1602_IIC1.SDA, U4.pin2
  N6: LCM1602_IIC1.SCL, U4.pin1
  N7: U2.pin1, R2.leg1
  N8: U2.pin2, R2.wiper
  N9: U2.pin3, R2.leg2
  N10: SP1.+, J5.pin1
  N11: SP1.-, J5.pin2
  N12: U9.SLEEVE, U10.pin3

notes:
  5V
  GND
  power amp in
  speed control
  audio output
  audio volume control 500KA
  speed control 100KB
  paddle input

custom parts:
  Electrolytic Capacitor top view: A small electrolytic capacitor breadboard top view for use on perf board
  Vertical Resistor: A generic resistor (0.25W)
  Wemos Lolin32lite: Wemos Lolinlite32 wifi and blue tooth board based on the ESP-32 cpu, digital I/Os 19, analog inputs 6, clock 240mhz, Flash 4Mbytes, lipo battery charger (500ma connection broken out on breadboard but not pcb), usb.
  LCM1602 IIC: I2C-Module to use a 1602 or 2004 LCD on with the wire.h libory Serial LCD Modul
  JST XH 3A Male: 2.54 Mm JST "XH" connector
  JST XH 2A male: JST XH-2A
  JST XH 4A 2.54mm: 4 Pin JST XH connector
